// Logisim project unidade_controle_microprogramada.circ as structural Verilog: 1 circuit, main circuit ControlUnit
module ControlUnit (
  input  [7:0] Opcode_In,
  input  cond_pass,
  output RegWrite_Out,
  output MemWrite_Out,
  output FlagsWrite_Out,
  output PCWrite_Out,
  output [1:0] PC_src_Out,
  output [1:0] wb_src_Out,
  output MemRead_Out,
  output [1:0] shift_ctl_Out,
  output [1:0] ALU_srcB_Out,
  output ALU_srcA_Out,
  output [1:0] invB_cin_Out,
  output [3:0] ALU_op_Out,
  output [1:0] reg_read_sel_Out
);

  wire clock_1_out, FlagsWrite, MemWrite, PCWrite, RegWrite;
  wire [1:0] useq_sel;
  wire [5:0] adder_1_out, Dispatch_out, multiplexer_1_out, next_uaddr, uPC_q;

  PLA #(.in_width(8), .out_width(6), .\table ("00000000 010000 # ADD\n00000000 010001 # SUB\n00000000 010010 # AND\n00000000 010011 # ORR\n00000000 010100 # CMP\n00000000 010101 # MOV\n00000000 100000 # LDR\n00000000 110000 # STR\n00000000 111111 # Branch (B)")) Dispatch (
    .in(Opcode_In), .out(Dispatch_out));
  Register #(.width(6)) uPC (.D(multiplexer_1_out), .clk(clock_1_out), .Q(uPC_q));  // open: en, clr
  Clock clock_1 (.out(clock_1_out));
  and and_1 (RegWrite_Out, RegWrite, cond_pass);
  and and_2 (MemWrite_Out, MemWrite, cond_pass);
  and and_3 (FlagsWrite_Out, FlagsWrite, cond_pass);
  and and_4 (PCWrite_Out, PCWrite, cond_pass);
  Adder #(.width(6)) adder_1 (.a(uPC_q), .b(6'b000001), .out(adder_1_out));  // open: cin, cout
  ROM #(.addrWidth(6), .dataWidth(30)) rom_1 (
    .addr(uPC_q),
    .data({useq_sel, next_uaddr, reg_read_sel_Out, ALU_op_Out, invB_cin_Out, ALU_srcA_Out, ALU_srcB_Out, shift_ctl_Out, MemRead_Out, MemWrite, wb_src_Out, RegWrite, FlagsWrite, PCWrite, PC_src_Out}));
  Multiplexer #(.select(2), .width(6)) multiplexer_1 (
    .in0(adder_1_out), .in1(next_uaddr), .in2(Dispatch_out), .out(multiplexer_1_out), .sel(useq_sel));  // open: in3

  // Other names for the same wires on the sheet: PC_src[1:0] = PC_src_Out; wb_src[1:0] = wb_src_Out;
  //   MemRead = MemRead_Out; shift_ctl[1:0] = shift_ctl_Out; ALU_srcB[1:0] = ALU_srcB_Out; ALU_srcA = ALU_srcA_Out;
  //   invB_cin[1:0] = invB_cin_Out; ALU_op[3:0] = ALU_op_Out; reg_read_sel[1:0] = reg_read_sel_Out

  // Notes on the sheet:
  //   contents of rom_1 (hex, n*v repeats v):
  //   3104 10000000 14*0 20000018 20008018 20020018 20030018 20008008 20040018 10*0 a00 100 20000030 13*0
  //   a00 20000080 13*0 20000005
endmodule
